// Digital circuit alu.dig as structural Verilog
module alu (
  input  [31:0] a,
  input  [31:0] b,
  input  [2:0] func,
  output [31:0] res,
  output zero
);

  wire [0:0] comparator_1_lt;
  wire [31:0] add_1_s, and_1_out, or_1_out, sub_1_s;

  Add #(.Bits(32)) add_1 (.a(a), .b(b), .c_i(1'b0), .s(add_1_s));  // open: c_o
  Sub #(.Bits(32)) sub_1 (.a(a), .b(b), .c_i(1'b0), .s(sub_1_s));  // open: c_o
  Comparator #(.Signed("true"), .Bits(32)) comparator_1 (.a(a), .b(b), .lt(comparator_1_lt[0]));  // open: gt, eq
  assign and_1_out = a & b;  // And and_1, 32 bits wide
  assign or_1_out = a | b;  // Or or_1, 32 bits wide
  Multiplexer #(.Bits(32), .Selector_Bits(3)) multiplexer_1 (
    .sel(func), .in_0(add_1_s), .in_1(sub_1_s), .in_2({{31{1'b0}}, comparator_1_lt[0]}), .in_3(and_1_out),
    .in_4(or_1_out), .in_5({32{1'b0}}), .in_6({32{1'b0}}), .in_7({32{1'b0}}), .out(res));
  Comparator #(.Bits(32)) comparator_2 (.a(res), .b({32{1'b0}}), .eq(zero));  // open: gt, lt
endmodule
