// Digital circuit control_unit_full.dig as structural Verilog
module control_unit_full (
  input  [5:0] opcode,
  input  [5:0] func,
  output jump,
  output Branch,
  output MemRead,
  output MemWrite,
  output MemToReg,
  output ALUSrc,
  output RegWrite,
  output RegDst,
  output InvOpcode,
  output [2:0] ALUFunc,
  output Bne
);

  wire add, \and , beq, bne_t, comparator_1_eq, jmp, lw, \or , slt, sub, sw;
  wire [3:0] priorityencoder_1_num;
  wire [5:0] multiplexer_1_out;

  Comparator #(.Bits(6)) comparator_1 (.a(opcode), .b({6{1'b0}}), .eq(comparator_1_eq));  // open: gt, lt
  Multiplexer #(.Bits(6)) multiplexer_1 (.sel(comparator_1_eq), .in_0({6{1'b0}}), .in_1(func), .out(multiplexer_1_out));
  Comparator #(.Bits(6)) u_lw (.a(opcode), .b(6'b100011), .eq(lw));  // open: gt, lt
  Comparator #(.Bits(6)) u_sw (.a(opcode), .b(6'b101011), .eq(sw));  // open: gt, lt
  Comparator #(.Bits(6)) u_beq (.a(opcode), .b(6'b000100), .eq(beq));  // open: gt, lt
  Comparator #(.Bits(6)) u_jmp (.a(opcode), .b(6'b000010), .eq(jmp));  // open: gt, lt
  Comparator #(.Bits(6)) u_bne (.a(opcode), .b(6'b000101), .eq(bne_t));  // open: gt, lt
  Comparator #(.Bits(6)) u_add (.a(multiplexer_1_out), .b(6'b100000), .eq(add));  // open: gt, lt
  Comparator #(.Bits(6)) u_sub (.a(multiplexer_1_out), .b(6'b100010), .eq(sub));  // open: gt, lt
  Comparator #(.Bits(6)) u_slt (.a(multiplexer_1_out), .b(6'b101010), .eq(slt));  // open: gt, lt
  Comparator #(.Bits(6)) u_and (.a(multiplexer_1_out), .b(6'b100100), .eq(\and ));  // open: gt, lt
  Comparator #(.Bits(6)) u_or (.a(multiplexer_1_out), .b(6'b100101), .eq(\or ));  // open: gt, lt
  PriorityEncoder #(.Selector_Bits(4)) priorityencoder_1 (
    .in0(lw), .in1(sw), .in2(beq), .in3(jmp), .in4(bne_t), .in5(add), .in6(sub), .in7(slt), .in8(\and ),
    .in9(\or ), .in10(1'b0), .in11(1'b0), .in12(1'b0), .in13(1'b0), .in14(1'b0), .in15(1'b0),
    .num(priorityencoder_1_num));  // open: any
  Multiplexer #(.Selector_Bits(4), .Bits(13)) multiplexer_2 (
    .sel(priorityencoder_1_num), .in_0(13'h74), .in_1(13'h28), .in_2(13'h202), .in_3(13'h1), .in_4(13'h1200),
    .in_5(13'hc0), .in_6(13'h2c0), .in_7(13'h4c0), .in_8(13'h6c0), .in_9(13'h8c0), .in_10({13{1'b0}}),
    .in_11({13{1'b0}}), .in_12({13{1'b0}}), .in_13({13{1'b0}}), .in_14({13{1'b0}}), .in_15({13{1'b0}}),
    .out({Bne, ALUFunc, InvOpcode, RegDst, RegWrite, ALUSrc, MemToReg, MemWrite, MemRead, Branch, jump}));

  // Other names for the same wires on the sheet: op[5:0] = opcode
endmodule
