// Digital circuit mips32soc.dig as structural Verilog
module mips32soc (
  input  clk,
  input  rst
);

  wire AluSrc, and_1_out, and_2_out, Bne, branch, isZero, jump, MemRead, MemToReg, MemWrite, not_1_out,
       or_1_out, RegDst, RegWrite;
  wire [1:0] PC_q;
  wire [2:0] control_unit_full_1_alufunc;
  wire [3:0] add_1_s_2;
  wire [4:0] multiplexer_4_out;
  wire [5:0] func;
  wire [7:0] alu_1_res_2, PC_q_2;
  wire [27:0] add_1_s;
  wire [31:0] add_2_s, alu_1_res, DataMem_d, multiplexer_1_out, multiplexer_2_out, multiplexer_3_out,
       multiplexer_5_out, multiplexer_6_out, registerfile_1_da, registerfile_1_db, sign_ex;
  wire [31:6] Instr;
  wire [31:10] PC_q_3;

  Multiplexer #(.Bits(32)) multiplexer_1 (
    .sel(rst), .in_0(multiplexer_3_out), .in_1({32{1'b0}}), .out(multiplexer_1_out));
  Register #(.Bits(32)) PC (.D(multiplexer_1_out), .C(clk), .en(1'b1), .Q({PC_q_3, PC_q_2, PC_q}));
  Add #(.Bits(32)) add_1 (.a({PC_q_3, PC_q_2, PC_q}), .b(32'h4), .c_i(1'b0), .s({add_1_s_2, add_1_s}));  // open: c_o
  and and_1 (and_1_out, branch, isZero);
  not not_1 (not_1_out, isZero);
  and and_2 (and_2_out, Bne, not_1_out);
  ROM #(.AddrBits(8), .Bits(32)) InstMem (.A(PC_q_2), .sel(1'b1), .D({Instr, func}));
  or or_1 (or_1_out, and_1_out, and_2_out);
  Add #(.Bits(32)) add_2 (.a({add_1_s_2, add_1_s}), .b({sign_ex[29:0], 2'b00}), .c_i(1'b0), .s(add_2_s));  // open: c_o
  Multiplexer #(.Bits(32)) multiplexer_2 (
    .sel(or_1_out), .in_0({add_1_s_2, add_1_s}), .in_1(add_2_s), .out(multiplexer_2_out));
  Multiplexer #(.Bits(32)) multiplexer_3 (
    .sel(jump), .in_0(multiplexer_2_out), .in_1({add_1_s_2, Instr[25:6], func, 2'b00}),
    .out(multiplexer_3_out));
  Multiplexer #(.Bits(5)) multiplexer_4 (
    .sel(RegDst), .in_0(Instr[20:16]), .in_1(Instr[15:11]), .out(multiplexer_4_out));
  control_unit_full control_unit_full_1 (
    .opcode(Instr[31:26]), .func(func), .jump(jump), .Branch(branch), .MemRead(MemRead), .MemWrite(MemWrite),
    .MemToReg(MemToReg), .ALUSrc(AluSrc), .RegWrite(RegWrite), .RegDst(RegDst),
    .ALUFunc(control_unit_full_1_alufunc), .Bne(Bne));  // open: InvOpcode
  BitExtender #(.inputBits(16), .outputBits(32)) bitextender_1 (.in({Instr[15:6], func}), .out(sign_ex));
  RegisterFile #(.AddrBits(5), .Bits(32)) registerfile_1 (
    .Din(multiplexer_6_out), .we(RegWrite), .Rw(multiplexer_4_out), .C(clk), .Ra(Instr[25:21]),
    .Rb(Instr[20:16]), .Da(registerfile_1_da), .Db(registerfile_1_db));
  Multiplexer #(.Bits(32)) multiplexer_5 (
    .sel(AluSrc), .in_0(registerfile_1_db), .in_1(sign_ex), .out(multiplexer_5_out));
  alu alu_1 (
    .a(registerfile_1_da), .b(multiplexer_5_out), .func(control_unit_full_1_alufunc),
    .res({alu_1_res[31:10], alu_1_res_2, alu_1_res[1:0]}), .zero(isZero));
  Multiplexer #(.Bits(32)) multiplexer_6 (
    .sel(MemToReg), .in_0({alu_1_res[31:10], alu_1_res_2, alu_1_res[1:0]}), .in_1(DataMem_d),
    .out(multiplexer_6_out));
  RAMDualPort #(.AddrBits(8), .Bits(32)) DataMem (
    .A(alu_1_res_2), .Din(registerfile_1_db), .str(MemWrite), .C(clk), .ld(MemRead), .D(DataMem_d));

  // Other names for the same wires on the sheet: Instr[5:0] = func

  // Notes on the sheet:
  //   contents of InstMem (hex, n*v repeats v):
  //   deadbeef,11111111,22222222,33333333,44444444,55555555,66666666,77777777,88888888,
  //   99999999
endmodule
